// Logisim project 5-Stage_Pipelined_CPU.circ as structural Verilog: 18 circuits, main circuit main
module main (
);

  wire Branch_EX, Branch_ID, Branch_Selector, CLK_out, func7_6__EX, func7_6__ID, func7_6__IF, IM_to_RF_EX,
       IM_to_RF_ID, IM_to_RF_MEM, IM_to_RF_WB, Load_EX, Load_ID, Load_MEM, Load_WB, Operand_B_Selector_EX,
       Operand_B_Selector_ID, RESET_out, Store_EX, Store_ID, Store_MEM;
  wire [1:0] Immediate_Selector, Next_PC_Selector_EX, Next_PC_Selector_ID, Next_PC_Selector_MEM,
       Operand_A_Selector_EX, Operand_A_Selector_ID;
  wire [2:0] ALU_Operations_Selector_EX, ALU_Operations_Selector_ID, func3_EX, func3_ID, func3_IF;
  wire [3:0] ALU_Controller;
  wire [4:0] rd_EX, rd_ID, rd_MEM, rd_WB, rs1_ID, rs2_ID;
  wire [6:0] opcode_ID;
  wire [11:0] DM_Address_out, IM_Address;
  wire [31:0] ALU_Data_EX, ALU_Data_MEM, ALU_Data_WB, DM_Data_MEM, DM_Data_MEM_in, DM_Data_MEM_out,
       DM_Data_WB, DM_to_RF, I_EX, I_ID, IM_Data_ID, IM_Data_IF, Immediate_EX, Immediate_ID, Jump_I_Type_EX,
       Jump_I_Type_MEM, Jump_SB_Type_EX, Jump_SB_Type_MEM, Next_PC, Operand_A, Operand_B, PC_4_EX, PC_4_ID,
       PC_4_IF, PC_4_MEM, PC_EX, PC_ID, PC_IF, PC_MEM, rs1_data_EX, rs1_data_ID, rs2_data_EX, rs2_data_ID,
       S_ID, SB_EX, SB_ID, U_ID, UJ_EX, UJ_ID, UJ_MEM;

  Clock CLK (.out(CLK_out));
  Register #(.width(32)) Program_Counter (
    .D(Next_PC), .Q({PC_IF[31:14], IM_Address, PC_IF[1:0]}), .clk(CLK_out), .clr(RESET_out));  // open: en
  Button RESET (.out(RESET_out));
  Adder #(.width(32)) adder_1 (
    .a({PC_IF[31:14], IM_Address, PC_IF[1:0]}), .b(32'h4), .out(PC_4_IF));  // open: cin, cout
  ROM #(.addrWidth(12), .dataWidth(32)) rom_1 (
    .addr(IM_Address), .data({IM_Data_IF[31], func7_6__IF, IM_Data_IF[29:15], func3_IF, IM_Data_IF[11:0]}));  // open: sel
  IF_ID if_id_1 (
    .opcode_IF(IM_Data_IF[6:0]), .rd_IF(IM_Data_IF[11:7]), .func3_IF(func3_IF), .rs1_IF(IM_Data_IF[19:15]),
    .rs2_IF(IM_Data_IF[24:20]), .func7_6__IF(func7_6__IF),
    .IM_Data_IF({IM_Data_IF[31], func7_6__IF, IM_Data_IF[29:15], func3_IF, IM_Data_IF[11:0]}),
    .opcode_ID(opcode_ID), .rd_ID(rd_ID), .func3_ID(func3_ID), .rs1_ID(rs1_ID), .rs2_ID(rs2_ID),
    .func7_6__ID(func7_6__ID), .IM_Data_ID(IM_Data_ID), .CLK(CLK_out),
    .PC_IF({PC_IF[31:14], IM_Address, PC_IF[1:0]}), .PC_ID(PC_ID), .PC_4_IF(PC_4_IF), .PC_4_ID(PC_4_ID));
  Control_Unit control_unit_1 (
    .Instruction_Memory(opcode_ID), .Write(IM_to_RF_ID), .Store(Store_ID), .Load(Load_ID),
    .Branch(Branch_ID), .Operand_A(Operand_A_Selector_ID), .Operand_B(Operand_B_Selector_ID),
    .Immediate(Immediate_Selector), .Next_PC(Next_PC_Selector_ID), .ALU_Operations(ALU_Operations_Selector_ID));
  Register_File register_file_1 (
    .Instruction_Memory(DM_to_RF), .Source_Register_2_2(rs2_data_ID), .EN(IM_to_RF_WB),
    .Destination_Register(rd_WB), .Source_Register_2(rs2_ID), .Source_Register_1_2(rs1_data_ID),
    .Source_Register_1(rs1_ID), .CLK(CLK_out));
  Immediate_Generator immediate_generator_1 (
    .Instruction_Memory(IM_Data_ID), .I_Type(I_ID), .S_Type(S_ID), .SB_Type(SB_ID), .U_Type(U_ID),
    .UJ_Type(UJ_ID), .PC(PC_ID));
  Multiplexer #(.select(2), .width(32), .enable("false")) multiplexer_1 (
    .in0(I_ID), .in1(U_ID), .in2(S_ID), .out(Immediate_ID), .sel(Immediate_Selector));  // open: in3
  ID_EX id_ex_1 (
    .rs1_data_ID(rs1_data_ID), .rs2_data_ID(rs2_data_ID), .I_Type_ID(I_ID), .UJ_Type_ID(UJ_ID),
    .rs2_data_EX(rs1_data_EX), .rs2_data_EX_2(rs2_data_EX), .I_Type_EX(I_EX), .UJ_Type_EX(UJ_EX),
    .CLK(CLK_out), .SB_Type_ID(SB_ID), .SB_Type_EX(SB_EX), .Immediate_ID(Immediate_ID),
    .Immediate_EX(Immediate_EX), .PC_ID(PC_ID), .PC_EX(PC_EX), .PC_4_ID(PC_4_ID), .PC_4_EX(PC_4_EX),
    .func3_ID(func3_ID), .func3_EX(func3_EX), .func7_6__ID(func7_6__ID), .func7_6__EX(func7_6__EX),
    .Store_ID(Store_ID), .Store_EX(Store_EX), .Load_ID(Load_ID), .Load_EX(Load_EX), .Branch_ID(Branch_ID),
    .Branch_EX(Branch_EX), .Operand_A_Selector_ID(Operand_A_Selector_ID),
    .Operand_A_Selector_EX(Operand_A_Selector_EX), .Operand_B_Selector_ID(Operand_B_Selector_ID),
    .Operand_B_Selector_EX(Operand_B_Selector_EX), .Next_PC_Selector_ID(Next_PC_Selector_ID),
    .Next_PC_Selector_EX(Next_PC_Selector_EX), .ALU_Operations_Selector_ID(ALU_Operations_Selector_ID),
    .ALU_Operations_Selector_EX(ALU_Operations_Selector_EX), .IM_to_RF_ID(IM_to_RF_ID),
    .IM_to_RF_EX(IM_to_RF_EX), .rd_ID(rd_ID), .rd_EX(rd_EX));
  Multiplexer #(.select(2), .width(32), .enable("false")) multiplexer_2 (
    .in0(rs1_data_EX), .in1(PC_4_EX), .in2(PC_EX), .in3({32{1'b0}}), .out(Operand_A),
    .sel(Operand_A_Selector_EX));
  Multiplexer #(.width(32), .enable("false")) multiplexer_3 (
    .in0(rs2_data_EX), .in1(Immediate_EX), .out(Operand_B), .sel(Operand_B_Selector_EX));
  ALU_Controller alu_controller_1 (
    .func_7_6th_Bit(func7_6__EX), .ALU_Operations_Selector(ALU_Operations_Selector_EX), .func_3(func3_EX),
    .ALU_Controller(ALU_Controller));
  ALU alu_1 (
    .Operation_Select(ALU_Controller), .Data_Memory(ALU_Data_EX), .Operand_A(Operand_A), .Operand_B(Operand_B));
  Branch_Selector branch_selector_1 (
    .func_3(func3_EX), .rs1(rs1_data_EX), .rs2(rs2_data_EX), .EN(Branch_EX), .O_P(Branch_Selector));
  Adder #(.width(32)) adder_2 (.a(I_EX), .b(rs1_data_EX), .out(Jump_I_Type_EX));  // open: cin, cout
  Multiplexer #(.width(32), .enable("false")) multiplexer_4 (
    .in0(PC_4_EX), .in1(SB_EX), .out(Jump_SB_Type_EX), .sel(Branch_Selector));
  EX_MEM ex_mem_1 (
    .ALU_Data_EX(ALU_Data_EX), .ALU_Data_MEM(ALU_Data_MEM), .CLK(CLK_out), .PC_EX(PC_EX), .PC_MEM(PC_MEM),
    .PC_4_EX(PC_4_EX), .PC_4_ID(PC_4_MEM), .IM_to_RF_EX(IM_to_RF_EX), .IM_to_RF_MEM(IM_to_RF_MEM),
    .Store_EX(Store_EX), .Store_MEM(Store_MEM), .Load_EX(Load_EX), .Load_MEM(Load_MEM),
    .Next_PC_Selector_EX(Next_PC_Selector_EX), .Next_PC_Selector_MEM(Next_PC_Selector_MEM),
    .rs2_data_EX(rs2_data_EX), .rs2_data_MEM(DM_Data_MEM_in), .UJ_Type_EX(UJ_EX), .UJ_Type_MEM(UJ_MEM),
    .Jump_I_Type_EX(Jump_I_Type_EX), .Jump_I_Type_MEM(Jump_I_Type_MEM), .Jump_SB_Type_EX(Jump_SB_Type_EX),
    .Jump_SB_Type_MEM(Jump_SB_Type_MEM), .rd_ID(rd_EX), .rd_EX(rd_MEM));
  Multiplexer #(.select(2), .width(32), .enable("false")) multiplexer_5 (
    .in0(PC_4_MEM), .in1(Jump_I_Type_MEM), .in2(Jump_SB_Type_MEM), .in3(UJ_MEM), .out(Next_PC),
    .sel(Next_PC_Selector_MEM));
  RAM #(.addrWidth(12), .dataWidth(32), .bus("separate")) ram_1 (
    .addr(ALU_Data_MEM[13:2]), .din(DM_Data_MEM_in), .data(DM_Data_MEM_out), .str(Store_MEM), .clk(CLK_out),
    .ld(Load_MEM));  // open: sel, clr
  MEM_WB mem_wb_1 (
    .DM_Data_MEM(DM_Data_MEM_out), .DM_Data_WB(DM_Data_WB), .CLK(CLK_out), .IM_to_RF_MEM(IM_to_RF_MEM),
    .IM_to_RF_WB(IM_to_RF_WB), .Load_MEM(Load_MEM), .Load_WB(Load_WB), .ALU_Data_MEM(ALU_Data_MEM),
    .ALU_Data_WB(ALU_Data_WB), .rd_ID(rd_MEM), .rd_EX(rd_WB));
  Multiplexer #(.width(32), .enable("false")) multiplexer_6 (
    .in0(ALU_Data_WB), .in1(DM_Data_WB), .out(DM_to_RF), .sel(Load_WB));
  // Probe on Next_PC
  // Probe on {PC_IF[31:14], IM_Address, PC_IF[1:0]}
  // Probe on PC_4_IF
  // Probe on IM_Address
  // Probe on {IM_Data_IF[31], func7_6__IF, IM_Data_IF[29:15], func3_IF, IM_Data_IF[11:0]}
  // Probe on IM_Data_IF[6:0]
  // Probe on IM_Data_IF[11:7]
  // Probe on func3_IF
  // Probe on IM_Data_IF[19:15]
  // Probe on IM_Data_IF[24:20]
  // Probe on func7_6__IF
  // Probe on PC_ID
  // Probe on PC_4_ID
  // Probe on IM_Data_ID
  // Probe on opcode_ID
  // Probe on rd_ID
  // Probe on func3_ID
  // Probe on rs1_ID
  // Probe on rs2_ID
  // Probe on func7_6__IF
  // Probe on IM_to_RF_ID
  // Probe on rd_ID
  // Probe on DM_to_RF
  // Probe on rs1_ID
  // Probe on rs1_data_ID
  // Probe on rs2_ID
  // Probe on rs2_data_ID
  // Probe on IM_Data_ID
  // Probe on PC_ID
  // Probe on I_ID
  // Probe on U_ID
  // Probe on S_ID
  // Probe on Immediate_Selector
  // Probe on Immediate_ID
  // Probe on Operand_A_Selector_ID
  // Probe on Operand_B_Selector_ID
  // Probe on ALU_Operations_Selector_ID
  // Probe on Store_ID
  // Probe on Load_ID
  // Probe on Branch_ID
  // Probe on SB_ID
  // Probe on UJ_ID
  // Probe on Next_PC_Selector_ID
  // Probe on PC_EX
  // Probe on PC_4_EX
  // Probe on rd_EX
  // Probe on func3_EX
  // Probe on func7_6__EX
  // Probe on IM_to_RF_EX
  // Probe on rd_EX
  // Probe on rs1_data_EX
  // Probe on rs2_data_EX
  // Probe on I_EX
  // Probe on Immediate_EX
  // Probe on rs1_data_EX
  // Probe on PC_4_EX
  // Probe on PC_EX
  // Probe on Operand_A_Selector_EX
  // Probe on Operand_A
  // Probe on rs2_data_EX
  // Probe on Immediate_ID
  // Probe on Operand_B_Selector_EX
  // Probe on Operand_B
  // Probe on func3_EX
  // Probe on func7_6__EX
  // Probe on ALU_Operations_Selector_EX
  // Probe on ALU_Controller
  // Probe on Operand_A
  // Probe on Operand_B
  // Probe on ALU_Controller
  // Probe on ALU_Data_EX
  // Probe on Store_EX
  // Probe on Load_EX
  // Probe on Branch_EX
  // Probe on rs1_data_EX
  // Probe on rs2_data_EX
  // Probe on func3_EX
  // Probe on Branch_Selector
  // Probe on I_EX
  // Probe on rs1_data_EX
  // Probe on Jump_I_Type_EX
  // Probe on PC_4_EX
  // Probe on SB_EX
  // Probe on Jump_SB_Type_EX
  // Probe on UJ_EX
  // Probe on Next_PC_Selector_EX
  // Probe on PC_MEM
  // Probe on PC_4_MEM
  // Probe on rd_MEM
  // Probe on IM_to_RF_MEM
  // Probe on rd_MEM
  // Probe on DM_Data_MEM_in
  // Probe on ALU_Data_MEM
  // Probe on Store_MEM
  // Probe on ALU_Data_MEM[13:2]
  // Probe on DM_Data_MEM_in
  // Probe on Load_MEM
  // Probe on DM_Address_out
  // Probe on DM_Data_MEM
  // Probe on Jump_I_Type_MEM
  // Probe on Jump_SB_Type_MEM
  // Probe on PC_4_MEM
  // Probe on Jump_I_Type_MEM
  // Probe on Jump_SB_Type_MEM
  // Probe on UJ_MEM
  // Probe on Next_PC_Selector_MEM
  // Probe on Next_PC
  // Probe on rd_WB
  // Probe on IM_to_RF_MEM
  // Probe on rd_WB
  // Probe on DM_to_RF
  // Probe on ALU_Data_WB
  // Probe on Load_MEM
  // Probe on ALU_Data_WB
  // Probe on DM_Data_WB
  // Probe on Load_MEM
  // Probe on DM_to_RF

  // Other names for the same wires on the sheet: DM_Address[11:0] = ALU_Data_MEM[13:2];
  //   opcode_IF[6:0] = IM_Data_IF[6:0]; rd_IF[4:0] = IM_Data_IF[11:7];
  //   IM_Data_IF (some bits) = {func7_6__IF, func3_IF}; rs1_IF[4:0] = IM_Data_IF[19:15];
  //   rs2_IF[4:0] = IM_Data_IF[24:20]; PC_IF[13:2] = IM_Address; rs2_data_MEM[31:0] = DM_Data_MEM_in

  // Notes on the sheet:
  //   Instruction Memory
  //   contents of rom_1 (hex, n*v repeats v):
  //   293 128293 502023 2303 ff5ff0ef
  //   Made By
  //   Ammar Bin Amir
  //   Data Memory
  //   RV32I 5-Stage Pipilining
endmodule

module Type_Decoder (
  input  [6:0] Opcode,
  output R_Type,
  output I_Type__lw,
  output I_Type__addi,
  output I_Type__jalr,
  output S_Type,
  output SB_Type,
  output U_Type__auipc,
  output U_Type__lui,
  output UJ_Type
);

  Comparator #(.width(7)) comparator_1 (.a(Opcode), .b(7'b0110011), .eq(R_Type));  // open: gt, lt
  Comparator #(.width(7)) comparator_2 (.a(Opcode), .b(7'b0000011), .eq(I_Type__lw));  // open: gt, lt
  Comparator #(.width(7)) comparator_3 (.a(Opcode), .b(7'b0010011), .eq(I_Type__addi));  // open: gt, lt
  Comparator #(.width(7)) comparator_4 (.a(Opcode), .b(7'b1100111), .eq(I_Type__jalr));  // open: gt, lt
  Comparator #(.width(7)) comparator_5 (.a(Opcode), .b(7'b0100011), .eq(S_Type));  // open: gt, lt
  Comparator #(.width(7)) comparator_6 (.a(Opcode), .b(7'b1100011), .eq(SB_Type));  // open: gt, lt
  Comparator #(.width(7)) comparator_7 (.a(Opcode), .b(7'b0010111), .eq(U_Type__auipc));  // open: gt, lt
  Comparator #(.width(7)) comparator_8 (.a(Opcode), .b(7'b0110111), .eq(U_Type__lui));  // open: gt, lt
  Comparator #(.width(7)) comparator_9 (.a(Opcode), .b(7'b1101111), .eq(UJ_Type));  // open: gt, lt
endmodule

module Control_Decoder (
  input  R_Type,
  input  I_Type_lw,
  input  I_Type_addi,
  input  I_Type_jalr,
  input  S_Type,
  input  SB_Type,
  input  U_Type_auipc,
  input  U_Type_lui,
  input  UJ_Type,
  output Write,
  output Store,
  output Load,
  output Branch,
  output [1:0] ALU_s_Operand_A,
  output ALU_s_Operand_B,
  output [1:0] Immediate_Selector,
  output [1:0] Next_PC_Selector,
  output [2:0] ALU_Operation_Selector
);

  or or_1 (Write, R_Type, I_Type_lw, I_Type_addi, I_Type_jalr, U_Type_auipc, U_Type_lui, UJ_Type);
  Operand_A_Selector_in_ALU operand_a_selector_in_alu_1 (
    .R(R_Type), .I__lw(I_Type_lw), .I__addi(I_Type_addi), .I__jalr(I_Type_jalr), .S(S_Type), .SB(SB_Type),
    .U__auipc(U_Type_auipc), .U__lui(U_Type_lui), .UJ(UJ_Type), .ZERO(1'b0),
    .Operand_A_Select(ALU_s_Operand_A));
  Operand_B_Selector_in_ALU operand_b_selector_in_alu_1 (
    .I__lw(I_Type_lw), .I__addi(I_Type_addi), .I__jalr(I_Type_jalr), .S(S_Type), .U__auipc(U_Type_auipc),
    .U__lui(U_Type_lui), .Operand_B_Select(ALU_s_Operand_B));
  Immediate_Selector_in_ALU immediate_selector_in_alu_1 (
    .I__lw(I_Type_lw), .I__addi(I_Type_addi), .I__jalr(I_Type_jalr), .S(S_Type), .U__auipc(U_Type_auipc),
    .U__lui(U_Type_lui), .Immediate_Select(Immediate_Selector));
  Next_PC_Selector next_pc_selector_1 (
    .I__jalr(SB_Type), .SB(I_Type_jalr), .UJ(UJ_Type), .Next_PC_Select(Next_PC_Selector));
  ALU_Operation_Selector alu_operation_selector_1 (
    .R(R_Type), .I__lw(I_Type_lw), .I__addi(I_Type_addi), .I__jalr(I_Type_jalr), .S(S_Type),
    .U__auipc(U_Type_auipc), .U__lui(U_Type_lui), .UJ(UJ_Type), .ALU_Operation_Select(ALU_Operation_Selector));

  assign Branch = SB_Type;
  assign Load = I_Type_lw;
  assign Store = S_Type;
endmodule

module Operand_A_Selector_in_ALU (
  input  R,
  input  I__lw,
  input  I__addi,
  input  I__jalr,
  input  S,
  input  SB,
  input  U__auipc,
  input  U__lui,
  input  UJ,
  input  ZERO,
  output [1:0] Operand_A_Select
);

  or or_1 (Operand_A_Select[0], ZERO, UJ, I__jalr);
  or or_2 (Operand_A_Select[1], ZERO, U__auipc);
endmodule

module Operand_B_Selector_in_ALU (
  input  I__lw,
  input  I__addi,
  input  I__jalr,
  input  S,
  input  U__auipc,
  input  U__lui,
  output Operand_B_Select
);

  or or_1 (Operand_B_Select, U__lui, U__auipc, S, I__jalr, I__addi, I__lw);
endmodule

module Immediate_Selector_in_ALU (
  input  I__lw,
  input  I__addi,
  input  I__jalr,
  input  S,
  input  U__auipc,
  input  U__lui,
  output [1:0] Immediate_Select
);

  wire not_1_out, not_2_out, not_3_out, not_4_out, not_5_out, not_6_out, not_7_out, not_8_out, not_9_out;

  not not_1 (not_1_out, I__lw);
  not not_2 (not_2_out, I__addi);
  not not_3 (not_3_out, I__jalr);
  not not_4 (not_4_out, S);
  not not_5 (not_5_out, I__lw);
  not not_6 (not_6_out, I__addi);
  not not_7 (not_7_out, I__jalr);
  not not_8 (not_8_out, U__auipc);
  not not_9 (not_9_out, U__lui);
  and and_1 (Immediate_Select[0], not_1_out, not_2_out, not_3_out, not_4_out);
  and and_2 (Immediate_Select[1], not_5_out, not_6_out, not_7_out, not_8_out, not_9_out);
endmodule

module Next_PC_Selector (
  input  I__jalr,
  input  SB,
  input  UJ,
  output [1:0] Next_PC_Select
);

  or or_1 (Next_PC_Select[0], UJ, SB);
  or or_2 (Next_PC_Select[1], UJ, I__jalr);
endmodule

module ALU_Operation_Selector (
  input  R,
  input  I__lw,
  input  I__addi,
  input  I__jalr,
  input  S,
  input  U__auipc,
  input  U__lui,
  input  UJ,
  output [2:0] ALU_Operation_Select
);

  or or_1 (ALU_Operation_Select[0], UJ, U__lui, U__auipc, S);
  or or_2 (ALU_Operation_Select[1], UJ, U__lui, I__jalr, I__addi);
  or or_3 (ALU_Operation_Select[2], UJ, U__auipc, I__jalr, I__lw);
endmodule

module Control_Unit (
  input  [6:0] Instruction_Memory,
  output Write,
  output Store,
  output Load,
  output Branch,
  output [1:0] Operand_A,
  output Operand_B,
  output [1:0] Immediate,
  output [1:0] Next_PC,
  output [2:0] ALU_Operations
);

  wire type_decoder_1_i_type__addi, type_decoder_1_i_type__jalr, type_decoder_1_i_type__lw,
       type_decoder_1_r_type, type_decoder_1_s_type, type_decoder_1_sb_type, type_decoder_1_u_type__auipc,
       type_decoder_1_u_type__lui, type_decoder_1_uj_type;

  Type_Decoder type_decoder_1 (
    .Opcode(Instruction_Memory), .R_Type(type_decoder_1_r_type), .I_Type__lw(type_decoder_1_i_type__lw),
    .I_Type__addi(type_decoder_1_i_type__addi), .I_Type__jalr(type_decoder_1_i_type__jalr),
    .S_Type(type_decoder_1_s_type), .SB_Type(type_decoder_1_sb_type),
    .U_Type__auipc(type_decoder_1_u_type__auipc), .U_Type__lui(type_decoder_1_u_type__lui),
    .UJ_Type(type_decoder_1_uj_type));
  Control_Decoder control_decoder_1 (
    .Write(Write), .Store(Store), .Load(Load), .Branch(Branch), .ALU_s_Operand_A(Operand_A),
    .ALU_s_Operand_B(Operand_B), .Immediate_Selector(Immediate), .Next_PC_Selector(Next_PC),
    .R_Type(type_decoder_1_r_type), .I_Type_lw(type_decoder_1_i_type__lw),
    .I_Type_addi(type_decoder_1_i_type__addi), .I_Type_jalr(type_decoder_1_i_type__jalr),
    .S_Type(type_decoder_1_s_type), .SB_Type(type_decoder_1_sb_type),
    .U_Type_auipc(type_decoder_1_u_type__auipc), .U_Type_lui(type_decoder_1_u_type__lui),
    .UJ_Type(type_decoder_1_uj_type), .ALU_Operation_Selector(ALU_Operations));
endmodule

module Register_File (
  input  [31:0] Instruction_Memory,
  input  EN,
  input  [4:0] Destination_Register,
  input  [4:0] Source_Register_1,
  input  [4:0] Source_Register_2,
  input  CLK,
  output [31:0] Source_Register_1_2,
  output [31:0] Source_Register_2_2
);

  wire decoder_1_out1, decoder_1_out2, decoder_1_out3, decoder_1_out4, decoder_1_out5, decoder_1_out6,
       decoder_1_out7, decoder_1_out8, decoder_1_out9, decoder_1_out10, decoder_1_out11, decoder_1_out12,
       decoder_1_out13, decoder_1_out14, decoder_1_out15, decoder_1_out16, decoder_1_out17, decoder_1_out18,
       decoder_1_out19, decoder_1_out20, decoder_1_out21, decoder_1_out22, decoder_1_out23, decoder_1_out24,
       decoder_1_out25, decoder_1_out26, decoder_1_out27, decoder_1_out28, decoder_1_out29, decoder_1_out30,
       decoder_1_out31;
  wire [31:0] register_1_q, register_2_q, register_3_q, register_4_q, register_5_q, register_6_q,
       register_7_q, register_8_q, register_9_q, register_10_q, register_11_q, register_12_q, register_13_q,
       register_14_q, register_15_q, register_16_q, register_17_q, register_18_q, register_19_q,
       register_20_q, register_21_q, register_22_q, register_23_q, register_24_q, register_25_q,
       register_26_q, register_27_q, register_28_q, register_29_q, register_30_q, register_31_q;

  Decoder #(.select(5), .disabled(0)) decoder_1 (
    .out1(decoder_1_out1), .out2(decoder_1_out2), .out3(decoder_1_out3), .out4(decoder_1_out4),
    .out5(decoder_1_out5), .out6(decoder_1_out6), .out7(decoder_1_out7), .out8(decoder_1_out8),
    .out9(decoder_1_out9), .out10(decoder_1_out10), .out11(decoder_1_out11), .out12(decoder_1_out12),
    .out13(decoder_1_out13), .out14(decoder_1_out14), .out15(decoder_1_out15), .out16(decoder_1_out16),
    .out17(decoder_1_out17), .out18(decoder_1_out18), .out19(decoder_1_out19), .out20(decoder_1_out20),
    .out21(decoder_1_out21), .out22(decoder_1_out22), .out23(decoder_1_out23), .out24(decoder_1_out24),
    .out25(decoder_1_out25), .out26(decoder_1_out26), .out27(decoder_1_out27), .out28(decoder_1_out28),
    .out29(decoder_1_out29), .out30(decoder_1_out30), .out31(decoder_1_out31), .sel(Destination_Register),
    .en(EN));  // open: out0
  Register #(.width(32)) register_1 (
    .D(Instruction_Memory), .en(decoder_1_out1), .Q(register_1_q), .clk(CLK));  // open: clr
  Register #(.width(32)) register_2 (
    .D(Instruction_Memory), .en(decoder_1_out2), .Q(register_2_q), .clk(CLK));  // open: clr
  Register #(.width(32)) register_3 (
    .D(Instruction_Memory), .en(decoder_1_out3), .Q(register_3_q), .clk(CLK));  // open: clr
  Register #(.width(32)) register_4 (
    .D(Instruction_Memory), .en(decoder_1_out4), .Q(register_4_q), .clk(CLK));  // open: clr
  Register #(.width(32)) register_5 (
    .D(Instruction_Memory), .en(decoder_1_out5), .Q(register_5_q), .clk(CLK));  // open: clr
  Register #(.width(32)) register_6 (
    .D(Instruction_Memory), .en(decoder_1_out6), .Q(register_6_q), .clk(CLK));  // open: clr
  Register #(.width(32)) register_7 (
    .D(Instruction_Memory), .en(decoder_1_out7), .Q(register_7_q), .clk(CLK));  // open: clr
  Register #(.width(32)) register_8 (
    .D(Instruction_Memory), .en(decoder_1_out8), .Q(register_8_q), .clk(CLK));  // open: clr
  Register #(.width(32)) register_9 (
    .D(Instruction_Memory), .en(decoder_1_out9), .Q(register_9_q), .clk(CLK));  // open: clr
  Register #(.width(32)) register_10 (
    .D(Instruction_Memory), .en(decoder_1_out10), .Q(register_10_q), .clk(CLK));  // open: clr
  Register #(.width(32)) register_11 (
    .D(Instruction_Memory), .en(decoder_1_out11), .Q(register_11_q), .clk(CLK));  // open: clr
  Register #(.width(32)) register_12 (
    .D(Instruction_Memory), .en(decoder_1_out12), .Q(register_12_q), .clk(CLK));  // open: clr
  Register #(.width(32)) register_13 (
    .D(Instruction_Memory), .en(decoder_1_out13), .Q(register_13_q), .clk(CLK));  // open: clr
  Register #(.width(32)) register_14 (
    .D(Instruction_Memory), .en(decoder_1_out14), .Q(register_14_q), .clk(CLK));  // open: clr
  Register #(.width(32)) register_15 (
    .D(Instruction_Memory), .en(decoder_1_out15), .Q(register_15_q), .clk(CLK));  // open: clr
  Register #(.width(32)) register_16 (
    .D(Instruction_Memory), .en(decoder_1_out16), .Q(register_16_q), .clk(CLK));  // open: clr
  Register #(.width(32)) register_17 (
    .D(Instruction_Memory), .en(decoder_1_out17), .Q(register_17_q), .clk(CLK));  // open: clr
  Register #(.width(32)) register_18 (
    .D(Instruction_Memory), .en(decoder_1_out18), .Q(register_18_q), .clk(CLK));  // open: clr
  Register #(.width(32)) register_19 (
    .D(Instruction_Memory), .en(decoder_1_out19), .Q(register_19_q), .clk(CLK));  // open: clr
  Register #(.width(32)) register_20 (
    .D(Instruction_Memory), .en(decoder_1_out20), .Q(register_20_q), .clk(CLK));  // open: clr
  Register #(.width(32)) register_21 (
    .D(Instruction_Memory), .en(decoder_1_out21), .Q(register_21_q), .clk(CLK));  // open: clr
  Register #(.width(32)) register_22 (
    .D(Instruction_Memory), .en(decoder_1_out22), .Q(register_22_q), .clk(CLK));  // open: clr
  Register #(.width(32)) register_23 (
    .D(Instruction_Memory), .en(decoder_1_out23), .Q(register_23_q), .clk(CLK));  // open: clr
  Register #(.width(32)) register_24 (
    .D(Instruction_Memory), .en(decoder_1_out24), .Q(register_24_q), .clk(CLK));  // open: clr
  Register #(.width(32)) register_25 (
    .D(Instruction_Memory), .en(decoder_1_out25), .Q(register_25_q), .clk(CLK));  // open: clr
  Register #(.width(32)) register_26 (
    .D(Instruction_Memory), .en(decoder_1_out26), .Q(register_26_q), .clk(CLK));  // open: clr
  Register #(.width(32)) register_27 (
    .D(Instruction_Memory), .en(decoder_1_out27), .Q(register_27_q), .clk(CLK));  // open: clr
  Register #(.width(32)) register_28 (
    .D(Instruction_Memory), .en(decoder_1_out28), .Q(register_28_q), .clk(CLK));  // open: clr
  Register #(.width(32)) register_29 (
    .D(Instruction_Memory), .en(decoder_1_out29), .Q(register_29_q), .clk(CLK));  // open: clr
  Register #(.width(32)) register_30 (
    .D(Instruction_Memory), .en(decoder_1_out30), .Q(register_30_q), .clk(CLK));  // open: clr
  Register #(.width(32)) register_31 (
    .D(Instruction_Memory), .en(decoder_1_out31), .Q(register_31_q), .clk(CLK));  // open: clr
  Multiplexer #(.select(5), .width(32), .enable("false")) multiplexer_1 (
    .in0({32{1'b0}}), .in1(register_1_q), .in2(register_2_q), .in3(register_3_q), .in4(register_4_q),
    .in5(register_5_q), .in6(register_6_q), .in7(register_7_q), .in8(register_8_q), .in9(register_9_q),
    .in10(register_10_q), .in11(register_11_q), .in12(register_12_q), .in13(register_13_q),
    .in14(register_14_q), .in15(register_15_q), .in16(register_16_q), .in17(register_17_q),
    .in18(register_18_q), .in19(register_19_q), .in20(register_20_q), .in21(register_21_q),
    .in22(register_22_q), .in23(register_23_q), .in24(register_24_q), .in25(register_25_q),
    .in26(register_26_q), .in27(register_27_q), .in28(register_28_q), .in29(register_29_q),
    .in30(register_30_q), .in31(register_31_q), .out(Source_Register_1_2), .sel(Source_Register_1));
  Multiplexer #(.select(5), .width(32), .enable("false")) multiplexer_2 (
    .in0({32{1'b0}}), .in1(register_1_q), .in2(register_2_q), .in3(register_3_q), .in4(register_4_q),
    .in5(register_5_q), .in6(register_6_q), .in7(register_7_q), .in8(register_8_q), .in9(register_9_q),
    .in10(register_10_q), .in11(register_11_q), .in12(register_12_q), .in13(register_13_q),
    .in14(register_14_q), .in15(register_15_q), .in16(register_16_q), .in17(register_17_q),
    .in18(register_18_q), .in19(register_19_q), .in20(register_20_q), .in21(register_21_q),
    .in22(register_22_q), .in23(register_23_q), .in24(register_24_q), .in25(register_25_q),
    .in26(register_26_q), .in27(register_27_q), .in28(register_28_q), .in29(register_29_q),
    .in30(register_30_q), .in31(register_31_q), .out(Source_Register_2_2), .sel(Source_Register_2));
endmodule

module Immediate_Generator (
  input  [31:0] Instruction_Memory,
  input  [31:0] PC,
  output [31:0] I_Type,
  output [31:0] S_Type,
  output [31:0] SB_Type,
  output [31:0] U_Type,
  output [31:0] UJ_Type
);

  wire [31:0] bit_extender_1_out, bit_extender_4_out, bit_extender_5_out;

  assign bit_extender_1_out = {{12{Instruction_Memory[31]}}, Instruction_Memory[31:12]};  // Bit_Extender bit_extender_1
  assign I_Type = {{20{Instruction_Memory[31]}}, Instruction_Memory[31:20]};  // Bit_Extender bit_extender_2
  assign S_Type = {{20{Instruction_Memory[31]}}, {Instruction_Memory[31:25], Instruction_Memory[11:7]}};  // Bit_Extender bit_extender_3
  assign bit_extender_4_out = {{19{Instruction_Memory[31]}}, {Instruction_Memory[31], Instruction_Memory[7], Instruction_Memory[30:25], Instruction_Memory[11:8], 1'b0}};  // Bit_Extender bit_extender_4
  assign bit_extender_5_out = {{11{Instruction_Memory[31]}}, {Instruction_Memory[31], Instruction_Memory[19:12], Instruction_Memory[20], Instruction_Memory[30:21], 1'b0}};  // Bit_Extender bit_extender_5
  Adder #(.width(32)) adder_1 (.a(bit_extender_4_out), .b(PC), .out(SB_Type));  // open: cin, cout
  Shifter #(.width(32)) shifter_1 (.in(bit_extender_1_out), .\dist (5'b01100), .out(U_Type));
  Adder #(.width(32)) adder_2 (.a(bit_extender_5_out), .b(PC), .out(UJ_Type));  // open: cin, cout
endmodule

module ALU_Controller (
  input  [2:0] ALU_Operations_Selector,
  input  func_7_6th_Bit,
  input  [2:0] func_3,
  output [3:0] ALU_Controller
);

  wire and_1_out, and_2_out, and_3_out, and_4_out, and_5_out, and_6_out, and_7_out, and_8_out, and_9_out,
       and_10_out, and_11_out, and_12_out, and_13_out, and_14_out, and_15_out, and_16_out, not_1_out,
       not_2_out, not_3_out, not_4_out, not_5_out, not_6_out, not_7_out, not_8_out, not_9_out, not_10_out,
       not_11_out, not_12_out, not_13_out, not_14_out, not_15_out, not_16_out, not_17_out, not_18_out,
       not_19_out, not_20_out, not_21_out, not_22_out, not_23_out, not_24_out, not_25_out, not_26_out,
       not_27_out, not_28_out, not_29_out, not_30_out, not_31_out;

  not not_1 (not_1_out, ALU_Operations_Selector[2]);
  not not_2 (not_2_out, func_3[2]);
  not not_3 (not_3_out, ALU_Operations_Selector[2]);
  not not_4 (not_4_out, func_3[1]);
  not not_5 (not_5_out, ALU_Operations_Selector[2]);
  not not_6 (not_6_out, func_7_6th_Bit);
  not not_7 (not_7_out, func_3[1]);
  not not_8 (not_8_out, ALU_Operations_Selector[2]);
  not not_9 (not_9_out, ALU_Operations_Selector[0]);
  not not_10 (not_10_out, func_3[2]);
  not not_11 (not_11_out, func_3[0]);
  not not_12 (not_12_out, ALU_Operations_Selector[2]);
  not not_13 (not_13_out, func_3[1]);
  not not_14 (not_14_out, func_3[0]);
  not not_15 (not_15_out, ALU_Operations_Selector[2]);
  not not_16 (not_16_out, ALU_Operations_Selector[0]);
  not not_17 (not_17_out, func_3[0]);
  not not_18 (not_18_out, ALU_Operations_Selector[2]);
  not not_19 (not_19_out, func_7_6th_Bit);
  not not_20 (not_20_out, ALU_Operations_Selector[2]);
  not not_21 (not_21_out, func_3[2]);
  not not_22 (not_22_out, func_3[1]);
  not not_23 (not_23_out, ALU_Operations_Selector[2]);
  not not_24 (not_24_out, ALU_Operations_Selector[0]);
  not not_25 (not_25_out, func_3[0]);
  not not_26 (not_26_out, ALU_Operations_Selector[1]);
  not not_27 (not_27_out, ALU_Operations_Selector[0]);
  not not_28 (not_28_out, func_3[1]);
  not not_29 (not_29_out, ALU_Operations_Selector[2]);
  not not_30 (not_30_out, func_3[1]);
  and and_1 (and_1_out, not_1_out, not_2_out, func_3[1], func_3[0]);
  and and_2 (and_2_out, not_3_out, func_7_6th_Bit, not_4_out, func_3[0]);
  and and_3 (and_3_out, ALU_Operations_Selector[1], ALU_Operations_Selector[0]);
  and and_4 (and_4_out, not_5_out, not_6_out, not_7_out, func_3[0]);
  and and_5 (and_5_out, not_8_out, not_9_out, not_10_out, func_3[1], not_11_out);
  and and_6 (and_6_out, not_12_out, func_3[2], not_13_out, not_14_out);
  and and_7 (and_7_out, ALU_Operations_Selector[1], ALU_Operations_Selector[0]);
  and and_8 (and_8_out, not_15_out, not_16_out, func_3[1], not_17_out);
  and and_9 (and_9_out, not_18_out, not_19_out, func_3[2], func_3[0]);
  not not_31 (not_31_out, ALU_Operations_Selector[2]);
  and and_10 (and_10_out, not_31_out, func_3[2], func_3[1]);
  and and_11 (and_11_out, ALU_Operations_Selector[1], ALU_Operations_Selector[0]);
  and and_12 (and_12_out, not_20_out, not_21_out, not_22_out, func_3[0]);
  and and_13 (and_13_out, not_23_out, not_24_out, func_3[1], not_25_out);
  and and_14 (and_14_out, not_26_out, not_27_out, func_7_6th_Bit, not_28_out);
  and and_15 (and_15_out, not_29_out, func_7_6th_Bit, not_30_out, func_3[0]);
  and and_16 (and_16_out, ALU_Operations_Selector[1], ALU_Operations_Selector[0]);
  or or_1 (ALU_Controller[0], and_1_out, and_2_out, and_3_out);
  or or_2 (ALU_Controller[1], and_4_out, and_5_out, and_6_out, and_7_out);
  or or_3 (ALU_Controller[2], and_8_out, and_9_out, and_10_out, and_11_out);
  or or_4 (ALU_Controller[3], and_12_out, and_13_out, and_14_out, and_15_out, and_16_out);
endmodule

module ALU (
  input  [3:0] Operation_Select,
  input  [31:0] Operand_A,
  input  [31:0] Operand_B,
  output [31:0] Data_Memory
);

  wire comparator_1_lt, comparator_2_lt;
  wire [31:0] adder_1_out, and_1_out, multiplexer_1_out, multiplexer_2_out, or_1_out, shifter_1_out,
       shifter_2_out, shifter_3_out, subtractor_1_out, xor_1_out;

  Adder #(.width(32)) adder_1 (.a(Operand_A), .b(Operand_B), .out(adder_1_out), .cin(1'b0));  // open: cout
  Subtractor #(.width(32)) subtractor_1 (
    .a(Operand_A), .b(Operand_B), .out(subtractor_1_out), .bin(1'b0));  // open: bout
  Shifter #(.width(32)) shifter_1 (.in(Operand_A), .\dist (Operand_B[4:0]), .out(shifter_1_out));
  Shifter #(.width(32), .shift("lr")) shifter_2 (.in(Operand_A), .\dist (Operand_B[4:0]), .out(shifter_2_out));
  Comparator #(.width(32)) comparator_1 (.a(Operand_A), .b(Operand_B), .lt(comparator_1_lt));  // open: gt, eq
  Comparator #(.width(32), .mode("unsigned")) comparator_2 (
    .a(Operand_A), .b(Operand_B), .lt(comparator_2_lt));  // open: gt, eq
  Shifter #(.width(32), .shift("ar")) shifter_3 (.in(Operand_A), .\dist (Operand_B[4:0]), .out(shifter_3_out));
  assign and_1_out = Operand_A & Operand_B;  // AND_Gate and_1, 32 bits wide
  assign or_1_out = Operand_A | Operand_B;  // OR_Gate or_1, 32 bits wide
  assign xor_1_out = Operand_A ^ Operand_B;  // XOR_Gate xor_1, 32 bits wide
  Multiplexer #(.width(32), .enable("false")) multiplexer_1 (
    .in0({32{1'b0}}), .in1(32'h1), .out(multiplexer_1_out), .sel(comparator_1_lt));
  Multiplexer #(.width(32), .enable("false")) multiplexer_2 (
    .in0({32{1'b0}}), .in1(32'h1), .out(multiplexer_2_out), .sel(comparator_2_lt));
  Multiplexer #(.select(4), .width(32), .enable("false")) multiplexer_3 (
    .in0(adder_1_out), .in1(subtractor_1_out), .in2(and_1_out), .in3(or_1_out), .in4(xor_1_out),
    .in5(shifter_1_out), .in6(shifter_2_out), .in7(multiplexer_1_out), .in8(multiplexer_2_out),
    .in9(shifter_3_out), .in15(Operand_B), .out(Data_Memory), .sel(Operation_Select));  // open: in10, in11, in12, in13, in14
endmodule

module Branch_Selector (
  input  EN,
  input  [2:0] func_3,
  input  [31:0] rs1,
  input  [31:0] rs2,
  output O_P
);

  wire comparator_1_eq, comparator_2_eq, comparator_3_lt, comparator_4_eq, comparator_4_gt, comparator_5_lt,
       comparator_6_eq, comparator_6_gt, not_1_out, or_1_out, or_2_out;

  Comparator #(.width(32)) comparator_1 (.a(rs1), .b(rs2), .eq(comparator_1_eq));  // open: gt, lt
  Comparator #(.width(32)) comparator_2 (.a(rs1), .b(rs2), .eq(comparator_2_eq));  // open: gt, lt
  Comparator #(.width(32)) comparator_3 (.a(rs1), .b(rs2), .lt(comparator_3_lt));  // open: gt, eq
  Comparator #(.width(32)) comparator_4 (.a(rs1), .b(rs2), .gt(comparator_4_gt), .eq(comparator_4_eq));  // open: lt
  Comparator #(.width(32), .mode("unsigned")) comparator_5 (.a(rs1), .b(rs2), .lt(comparator_5_lt));  // open: gt, eq
  Comparator #(.width(32), .mode("unsigned")) comparator_6 (
    .a(rs1), .b(rs2), .gt(comparator_6_gt), .eq(comparator_6_eq));  // open: lt
  not not_1 (not_1_out, comparator_2_eq);
  or or_1 (or_1_out, comparator_4_gt, comparator_4_eq);
  or or_2 (or_2_out, comparator_6_gt, comparator_6_eq);
  Multiplexer #(.select(3)) multiplexer_1 (
    .in0(comparator_1_eq), .in1(not_1_out), .in4(comparator_3_lt), .in5(or_1_out), .in6(comparator_5_lt),
    .in7(or_2_out), .out(O_P), .sel(func_3), .en(EN));  // open: in2, in3
endmodule

module IF_ID (
  input  [31:0] PC_IF,
  input  [31:0] PC_4_IF,
  input  [6:0] opcode_IF,
  input  [4:0] rd_IF,
  input  [2:0] func3_IF,
  input  [4:0] rs1_IF,
  input  [4:0] rs2_IF,
  input  func7_6__IF,
  input  [31:0] IM_Data_IF,
  input  CLK,
  output [31:0] PC_ID,
  output [31:0] PC_4_ID,
  output [6:0] opcode_ID,
  output [4:0] rd_ID,
  output [2:0] func3_ID,
  output [4:0] rs1_ID,
  output [4:0] rs2_ID,
  output func7_6__ID,
  output [31:0] IM_Data_ID
);

  Register #(.width(32)) PC (.D(PC_IF), .Q(PC_ID), .clk(CLK));  // open: en, clr
  Register #(.width(32)) PC_4 (.D(PC_4_IF), .Q(PC_4_ID), .clk(CLK));  // open: en, clr
  Register #(.width(7)) opcode (.D(opcode_IF), .Q(opcode_ID), .clk(CLK));  // open: en, clr
  Register #(.width(5)) rd (.D(rd_IF), .Q(rd_ID), .clk(CLK));  // open: en, clr
  Register #(.width(3)) func3 (.D(func3_IF), .Q(func3_ID), .clk(CLK));  // open: en, clr
  Register #(.width(5)) rs1 (.D(rs1_IF), .Q(rs1_ID), .clk(CLK));  // open: en, clr
  Register #(.width(5)) rs2 (.D(rs2_IF), .Q(rs2_ID), .clk(CLK));  // open: en, clr
  Register #(.width(1)) func7_6 (.D(func7_6__IF), .Q(func7_6__ID), .clk(CLK));  // open: en, clr
  Register #(.width(32)) IM_Data (.D(IM_Data_IF), .Q(IM_Data_ID), .clk(CLK));  // open: en, clr
endmodule

module ID_EX (
  input  [31:0] PC_ID,
  input  [31:0] PC_4_ID,
  input  [4:0] rd_ID,
  input  [2:0] func3_ID,
  input  func7_6__ID,
  input  IM_to_RF_ID,
  input  Store_ID,
  input  Load_ID,
  input  Branch_ID,
  input  [1:0] Operand_A_Selector_ID,
  input  Operand_B_Selector_ID,
  input  [1:0] Next_PC_Selector_ID,
  input  [2:0] ALU_Operations_Selector_ID,
  input  [31:0] rs1_data_ID,
  input  [31:0] rs2_data_ID,
  input  [31:0] I_Type_ID,
  input  [31:0] SB_Type_ID,
  input  [31:0] UJ_Type_ID,
  input  [31:0] Immediate_ID,
  input  CLK,
  output [31:0] PC_EX,
  output [31:0] PC_4_EX,
  output [4:0] rd_EX,
  output [2:0] func3_EX,
  output func7_6__EX,
  output IM_to_RF_EX,
  output Store_EX,
  output Load_EX,
  output Branch_EX,
  output [1:0] Operand_A_Selector_EX,
  output Operand_B_Selector_EX,
  output [1:0] Next_PC_Selector_EX,
  output [2:0] ALU_Operations_Selector_EX,
  output [31:0] rs2_data_EX,
  output [31:0] rs2_data_EX_2,
  output [31:0] I_Type_EX,
  output [31:0] SB_Type_EX,
  output [31:0] UJ_Type_EX,
  output [31:0] Immediate_EX
);

  Register #(.width(32)) PC (.D(PC_ID), .Q(PC_EX), .clk(CLK));  // open: en, clr
  Register #(.width(32)) PC_4 (.D(PC_4_ID), .Q(PC_4_EX), .clk(CLK));  // open: en, clr
  Register #(.width(5)) rd (.D(rd_ID), .Q(rd_EX), .clk(CLK));  // open: en, clr
  Register #(.width(3)) func3 (.D(func3_ID), .Q(func3_EX), .clk(CLK));  // open: en, clr
  Register #(.width(1)) func7_6 (.D(func7_6__ID), .Q(func7_6__EX), .clk(CLK));  // open: en, clr
  Register #(.width(1)) IM_to_RF (.D(IM_to_RF_ID), .Q(IM_to_RF_EX), .clk(CLK));  // open: en, clr
  Register #(.width(1)) Store (.D(Store_ID), .Q(Store_EX), .clk(CLK));  // open: en, clr
  Register #(.width(1)) func7_6_2 (.D(Load_ID), .Q(Load_EX), .clk(CLK));  // open: en, clr
  Register #(.width(1)) Branch (.D(Branch_ID), .Q(Branch_EX), .clk(CLK));  // open: en, clr
  Register #(.width(2)) Operand_A_Selector (
    .D(Operand_A_Selector_ID), .Q(Operand_A_Selector_EX), .clk(CLK));  // open: en, clr
  Register #(.width(1)) Operand_B_Selector (
    .D(Operand_B_Selector_ID), .Q(Operand_B_Selector_EX), .clk(CLK));  // open: en, clr
  Register #(.width(2)) Next_PC_Selector (
    .D(Next_PC_Selector_ID), .Q(Next_PC_Selector_EX), .clk(CLK));  // open: en, clr
  Register #(.width(3)) ALU_Operations_Selector (
    .D(ALU_Operations_Selector_ID), .Q(ALU_Operations_Selector_EX), .clk(CLK));  // open: en, clr
  Register #(.width(32)) rs1_data (.D(rs1_data_ID), .Q(rs2_data_EX), .clk(CLK));  // open: en, clr
  Register #(.width(32)) rs2_data (.D(rs2_data_ID), .Q(rs2_data_EX_2), .clk(CLK));  // open: en, clr
  Register #(.width(32)) I_Type (.D(I_Type_ID), .Q(I_Type_EX), .clk(CLK));  // open: en, clr
  Register #(.width(32)) SB_Type (.D(SB_Type_ID), .Q(SB_Type_EX), .clk(CLK));  // open: en, clr
  Register #(.width(32)) UJ_Type (.D(UJ_Type_ID), .Q(UJ_Type_EX), .clk(CLK));  // open: en, clr
  Register #(.width(32)) Immediate (.D(Immediate_ID), .Q(Immediate_EX), .clk(CLK));  // open: en, clr
endmodule

module EX_MEM (
  input  [31:0] PC_EX,
  input  [31:0] PC_4_EX,
  input  [4:0] rd_ID,
  input  IM_to_RF_EX,
  input  Store_EX,
  input  Load_EX,
  input  [1:0] Next_PC_Selector_EX,
  input  [31:0] rs2_data_EX,
  input  [31:0] UJ_Type_EX,
  input  [31:0] ALU_Data_EX,
  input  [31:0] Jump_I_Type_EX,
  input  [31:0] Jump_SB_Type_EX,
  input  CLK,
  output [31:0] PC_MEM,
  output [31:0] PC_4_ID,
  output [4:0] rd_EX,
  output IM_to_RF_MEM,
  output Store_MEM,
  output Load_MEM,
  output [1:0] Next_PC_Selector_MEM,
  output [31:0] rs2_data_MEM,
  output [31:0] UJ_Type_MEM,
  output [31:0] ALU_Data_MEM,
  output [31:0] Jump_I_Type_MEM,
  output [31:0] Jump_SB_Type_MEM
);

  Register #(.width(32)) PC (.D(PC_EX), .Q(PC_MEM), .clk(CLK));  // open: en, clr
  Register #(.width(32)) PC_4 (.D(PC_4_EX), .Q(PC_4_ID), .clk(CLK));  // open: en, clr
  Register #(.width(5)) rd (.D(rd_ID), .Q(rd_EX), .clk(CLK));  // open: en, clr
  Register #(.width(1)) IM_to_RF (.D(IM_to_RF_EX), .Q(IM_to_RF_MEM), .clk(CLK));  // open: en, clr
  Register #(.width(1)) Store (.D(Store_EX), .Q(Store_MEM), .clk(CLK));  // open: en, clr
  Register #(.width(1)) func7_6 (.D(Load_EX), .Q(Load_MEM), .clk(CLK));  // open: en, clr
  Register #(.width(2)) Next_PC_Selector (
    .D(Next_PC_Selector_EX), .Q(Next_PC_Selector_MEM), .clk(CLK));  // open: en, clr
  Register #(.width(32)) rs2_data (.D(rs2_data_EX), .Q(rs2_data_MEM), .clk(CLK));  // open: en, clr
  Register #(.width(32)) UJ_Type (.D(UJ_Type_EX), .Q(UJ_Type_MEM), .clk(CLK));  // open: en, clr
  Register #(.width(32)) ALU_Data (.D(ALU_Data_EX), .Q(ALU_Data_MEM), .clk(CLK));  // open: en, clr
  Register #(.width(32)) Jump_I_Type (.D(Jump_I_Type_EX), .Q(Jump_I_Type_MEM), .clk(CLK));  // open: en, clr
  Register #(.width(32)) Jump_SB_Type (.D(Jump_SB_Type_EX), .Q(Jump_SB_Type_MEM), .clk(CLK));  // open: en, clr
endmodule

module MEM_WB (
  input  [4:0] rd_ID,
  input  IM_to_RF_MEM,
  input  Load_MEM,
  input  [31:0] ALU_Data_MEM,
  input  [31:0] DM_Data_MEM,
  input  CLK,
  output [4:0] rd_EX,
  output IM_to_RF_WB,
  output Load_WB,
  output [31:0] ALU_Data_WB,
  output [31:0] DM_Data_WB
);

  Register #(.width(5)) rd (.D(rd_ID), .Q(rd_EX), .clk(CLK));  // open: en, clr
  Register #(.width(1)) IM_to_RF (.D(IM_to_RF_MEM), .Q(IM_to_RF_WB), .clk(CLK));  // open: en, clr
  Register #(.width(1)) Load (.D(Load_MEM), .Q(Load_WB), .clk(CLK));  // open: en, clr
  Register #(.width(32)) ALU_Data (.D(ALU_Data_MEM), .Q(ALU_Data_WB), .clk(CLK));  // open: en, clr
  Register #(.width(32)) DM_Data (.D(DM_Data_MEM), .Q(DM_Data_WB), .clk(CLK));  // open: en, clr
endmodule
